# Fritzing sketch Digital Tug of War With Sound (saved by Fritzing 0.9.3b)
breadboards: 1

parts:
  LED1 = RGB LED (com. cathode, rgb) [package="5 mm [THT]"]
  S1 = Pushbutton [package="[THT]"]
  S2 = Pushbutton [package="[THT]"]
  S3 = Pushbutton [package="[THT]"]
  S4 = Pushbutton [package="[THT]"]
  LED2 = LED - 5mm [color="Red (633nm)" package="5 mm [THT]"]
  LED3 = LED - 5mm [color="Red (633nm)" package="5 mm [THT]"]
  LED4 = LED - 5mm [color="Yellow (595nm)" package="5 mm [THT]"]
  LED5 = LED - 5mm [color="Yellow (595nm)" package="5 mm [THT]"]
  Part1 = Arduino Uno (Rev3) - ICSP
  R2 = Resistor [tolerance=±1% resistance=220 package=THT]
  R1 = Resistor [tolerance=±1% resistance=220 package=THT]
  R3 = Resistor [tolerance=±1% resistance=10k package=THT]
  R4 = Resistor [tolerance=±1% resistance=10k package=THT]
  R5 = Resistor [tolerance=±1% resistance=10k package=THT]
  R6 = Resistor [tolerance=±1% resistance=10k package=THT]
  J1 = Piezo Speaker
  R7 = Resistor [tolerance=±1% resistance=220 package=THT]

nets:
  N1: LED1.red_anode, Part1.D9_PWM
  N2: LED1.common_cathode, Part1.D10_PWM/SS
  N3: LED1.green_anode, Part1.D11_PWM/MOSI
  N4: LED1.blue_anode, Part1.GND, R2.Pin_0, R1.Pin_0, R3.Pin_0, R4.Pin_0, R5.Pin_0, R6.Pin_0, R7.Pin_0
  N5: S1.Pin_1, S1.Pin_2, S2.Pin_1, S2.Pin_2, S3.Pin_3, S3.Pin_4, S4.Pin_3, S4.Pin_4, Part1.5V, R6.Pin_1
  N6: S1.Pin_3, S1.Pin_4, Part1.D8
  N7: S2.Pin_3, S2.Pin_4, Part1.D7, R5.Pin_1
  N8: S3.Pin_1, S3.Pin_2, Part1.D4, R3.Pin_1
  N9: S4.Pin_1, S4.Pin_2, Part1.D5_PWM, R4.Pin_1
  N10: LED2.cathode, LED3.cathode, R1.Pin_1
  N11: LED2.anode, Part1.D13/SCK
  N12: LED3.anode, Part1.D12/MISO
  N13: LED4.cathode, LED5.cathode, R2.Pin_1
  N14: LED4.anode, Part1.D2
  N15: LED5.anode, Part1.D3_PWM
  N16: Part1.D6_PWM, J1.pin2
  N17: J1.pin1, R7.Pin_1
