# Fritzing sketch Keypad Music Box (saved by Fritzing 0.9.3b)
breadboards: 1
perfboards: 1

parts:
  Part1 = Arduino Uno (Rev3)
  S1 = Pushbutton [package="[THT]"]
  S2 = Pushbutton [package="[THT]"]
  S3 = Pushbutton [package="[THT]"]
  S4 = Pushbutton [package="[THT]"]
  S5 = Pushbutton [package="[THT]"]
  S6 = Pushbutton [package="[THT]"]
  S7 = Pushbutton [package="[THT]"]
  S8 = Pushbutton [package="[THT]"]
  S9 = Pushbutton [package="[THT]"]
  S10 = Pushbutton [package="[THT]"]
  S11 = Pushbutton [package="[THT]"]
  S12 = Pushbutton [package="[THT]"]
  S13 = Pushbutton [package="[THT]"]
  S14 = Pushbutton [package="[THT]"]
  S15 = Pushbutton [package="[THT]"]
  S16 = Pushbutton [package="[THT]"]
  J1 = Piezo Speaker
  R1 = Resistor [tolerance=±1% resistance=220 package=THT]
  R2 = Photocell (LDR) [package=THT]
  R3 = Resistor [tolerance=±1% resistance=10k package=THT]

nets:
  N1: Part1.A0, R2.pin_0, R3.Pin_1
  N2: Part1.D3_PWM, J1.pin2
  N3: Part1.5V, R2.pin_1
  N4: Part1.GND, R1.Pin_0, R3.Pin_0
  N5: S1.Pin_1, S1.Pin_2
  N6: S1.Pin_3, S1.Pin_4
  N7: S2.Pin_1, S2.Pin_2
  N8: S2.Pin_3, S2.Pin_4
  N9: S3.Pin_1, S3.Pin_2
  N10: S3.Pin_3, S3.Pin_4
  N11: S4.Pin_1, S4.Pin_2
  N12: S4.Pin_3, S4.Pin_4
  N13: S5.Pin_1, S5.Pin_2
  N14: S5.Pin_3, S5.Pin_4
  N15: S6.Pin_1, S6.Pin_2
  N16: S6.Pin_3, S6.Pin_4
  N17: S7.Pin_1, S7.Pin_2
  N18: S7.Pin_3, S7.Pin_4
  N19: S8.Pin_1, S8.Pin_2
  N20: S8.Pin_3, S8.Pin_4
  N21: S9.Pin_1, S9.Pin_2
  N22: S9.Pin_3, S9.Pin_4
  N23: S10.Pin_1, S10.Pin_2
  N24: S10.Pin_3, S10.Pin_4
  N25: S11.Pin_1, S11.Pin_2
  N26: S11.Pin_3, S11.Pin_4
  N27: S12.Pin_1, S12.Pin_2
  N28: S12.Pin_3, S12.Pin_4
  N29: S13.Pin_1, S13.Pin_2
  N30: S13.Pin_3, S13.Pin_4
  N31: S14.Pin_1, S14.Pin_2
  N32: S14.Pin_3, S14.Pin_4
  N33: S15.Pin_1, S15.Pin_2
  N34: S15.Pin_3, S15.Pin_4
  N35: S16.Pin_1, S16.Pin_2
  N36: S16.Pin_3, S16.Pin_4
  N37: J1.pin1, R1.Pin_1

notes:
  R4 | R3 | R2 | R1 | C1 | C2 | C3 | C4
